// Digital circuit KombinatorischeSchaltung.dig as structural Verilog
module KombinatorischeSchaltung (
  input  [7:0] S_equenz,
  output MDR_in,
  output MDR_out,
  output MAR_in,
  output IR_in,
  output IR_op_out,
  output IP_in,
  output IP_out,
  output R_in,
  output R_out,
  output [1:0] SR_eq_ROPx,
  output B_in,
  output Y_in,
  output Y_out,
  output A_in,
  output ALU_out,
  output [3:0] F_eq_x,
  output WR,
  output RD,
  output RDY,
  output Ca,
  output _0,
  output out_22,
  output [7:0] NA,
  output R,
  output De,
  output WRDY
);

  wire demultiplexer_1_out_0, demultiplexer_1_out_1, demultiplexer_1_out_2, demultiplexer_1_out_3,
       demultiplexer_1_out_4, demultiplexer_1_out_5, demultiplexer_1_out_6, demultiplexer_1_out_7,
       demultiplexer_1_out_8, demultiplexer_1_out_9, demultiplexer_1_out_10, demultiplexer_1_out_11,
       demultiplexer_1_out_12, demultiplexer_1_out_13;

  Demultiplexer #(.Selector_Bits(4)) demultiplexer_1 (
    .sel(S_equenz[3:0]), .in(1'b1), .out_0(demultiplexer_1_out_0), .out_1(demultiplexer_1_out_1),
    .out_2(demultiplexer_1_out_2), .out_3(demultiplexer_1_out_3), .out_4(demultiplexer_1_out_4),
    .out_5(demultiplexer_1_out_5), .out_6(demultiplexer_1_out_6), .out_7(demultiplexer_1_out_7),
    .out_8(demultiplexer_1_out_8), .out_9(demultiplexer_1_out_9), .out_10(demultiplexer_1_out_10),
    .out_11(demultiplexer_1_out_11), .out_12(demultiplexer_1_out_12), .out_13(demultiplexer_1_out_13));  // open: out_14, out_15
  PullDown pulldown_1 (.out(MDR_in));
  assign MDR_in = demultiplexer_1_out_0 ? 1'b1 : 1'bz;  // Driver driver_1
  assign MDR_out = demultiplexer_1_out_2 ? 1'b1 : 1'bz;  // Driver driver_2
  PullDown pulldown_2 (.out(MDR_out));
  assign MAR_in = demultiplexer_1_out_0 ? 1'b1 : 1'bz;  // Driver driver_3
  PullDown pulldown_3 (.out(MAR_in));
  assign IR_in = demultiplexer_1_out_2 ? 1'b1 : 1'bz;  // Driver driver_4
  PullDown pulldown_4 (.out(IR_in));
  PullDown pulldown_5 (.out(1'b0));
  assign IP_in = demultiplexer_1_out_1 ? 1'b1 : 1'bz;  // Driver driver_5
  PullDown pulldown_6 (.out(IP_in));
  assign IP_out = demultiplexer_1_out_0 ? 1'b1 : 1'bz;  // Driver driver_6
  PullDown pulldown_7 (.out(IP_out));
  PullDown pulldown_8 (.out(R_in));
  PullDown pulldown_9 (.out(R_out));
  PullDown #(.Bits(2)) pulldown_10 (.out(SR_eq_ROPx));
  PullDown pulldown_11 (.out(1'b0));
  PullDown pulldown_12 (.out(1'b0));
  PullDown pulldown_13 (.out(B_in));
  assign A_in = demultiplexer_1_out_0 ? 1'b1 : 1'bz;  // Driver driver_7
  PullDown pulldown_14 (.out(A_in));
  assign ALU_out = demultiplexer_1_out_1 ? 1'b1 : 1'bz;  // Driver driver_8
  PullDown pulldown_15 (.out(ALU_out));
  assign F_eq_x = demultiplexer_1_out_0 ? 4'b0110 : 4'bz;  // Driver driver_9
  PullDown #(.Bits(4)) pulldown_16 (.out(F_eq_x));
  PullDown pulldown_17 (.out(1'b0));
  PullDown pulldown_18 (.out(1'b0));
  PullDown pulldown_19 (.out(1'b0));
  PullDown pulldown_20 (.out(1'b0));
  PullDown pulldown_21 (.out(RD));
  assign RD = demultiplexer_1_out_0 ? 1'b1 : 1'bz;  // Driver driver_10
  PullDown pulldown_22 (.out(1'b0));
  PullDown #(.Bits(8)) pulldown_23 (.out({8{1'b0}}));
  PullDown pulldown_24 (.out(R));
  PullDown pulldown_25 (.out(De));
  assign De = demultiplexer_1_out_2 ? 1'b1 : 1'bz;  // Driver driver_11
  assign WRDY = demultiplexer_1_out_1 ? 1'b1 : 1'bz;  // Driver driver_12
  PullDown pulldown_26 (.out(WRDY));

  assign _0 = 1'b0;
  assign Ca = 1'b0;
  assign IR_op_out = 1'b0;
  assign NA = {8{1'b0}};
  assign out_22 = 1'b0;
  assign RDY = 1'b0;
  assign WR = 1'b0;
  assign Y_in = 1'b0;
  assign Y_out = 1'b0;

  // Notes on the sheet:
  //   0 FETCH
  //   3 ADD R2 = R2 + R1
endmodule
